// Logisim project cpu.circ as structural Verilog: 7 circuits, main circuit CPU
module CPU (
  output [47:0] cpu_out,
  output halt
);

  wire alu_1_negative, alu_1_overflow, alu_1_zero, and_2_out, and_3_out, and_4_out, clk_out, decoder_1_out0,
       decoder_1_out1, decoder_1_out2, decoder_1_out3, decoder_1_out4, decoder_2_out1, decoder_2_out2,
       decoder_2_out3, fulladder_1_cout, fulladder_2_cout, multiplexer_5_out, nor_1_out, not_1_out,
       not_2_out, not_3_out, not_4_out, or_1_out, or_2_out, reset_out, xor_1_out;
  wire [2:0] and_1_out, bit_extender_1_out, fulladder_1_s, multiplexer_2_out, multiplexer_4_out, register_1_q;
  wire [15:0] add_sixteen_1_s, alu_1_c, bit_extender_2_out, bit_extender_3_out, InsMem_data,
       multiplexer_1_out, multiplexer_3_out, multiplexer_6_out, RA_q, ram_1_dout, RB_q, RD_q,
       registerfile_1_a, registerfile_1_b, RW_q;

  Clock clk (.out(clk_out));
  Button reset (.out(reset_out));
  not not_1 (not_1_out, decoder_1_out4);
  assign bit_extender_1_out = {{2{not_1_out}}, not_1_out};  // Bit_Extender bit_extender_1
  Multiplexer #(.width(16)) multiplexer_1 (
    .in0(16'h1), .in1(bit_extender_2_out), .out(multiplexer_1_out), .sel(and_2_out));
  assign bit_extender_2_out = {{13{cpu_out[25]}}, cpu_out[25:23]};  // Bit_Extender bit_extender_2
  assign and_1_out = bit_extender_1_out & fulladder_1_s;  // AND_Gate and_1, 3 bits wide
  Register #(.width(3)) register_1 (.D(and_1_out), .en(1'b1), .clk(clk_out), .Q(register_1_q), .clr(reset_out));
  or or_1 (or_1_out, and_2_out, decoder_1_out0);
  fulladder fulladder_1 (.A(register_1_q[0]), .B(1'b1), .Cin(1'b0), .S(fulladder_1_s[0]), .Cout(fulladder_1_cout));
  fulladder fulladder_2 (
    .A(register_1_q[1]), .B(1'b0), .Cin(fulladder_1_cout), .S(fulladder_1_s[1]), .Cout(fulladder_2_cout));
  fulladder fulladder_3 (.A(register_1_q[2]), .B(1'b0), .Cin(fulladder_2_cout), .S(fulladder_1_s[2]));  // open: Cout
  Register #(.width(16)) PC (.D(add_sixteen_1_s), .en(or_1_out), .clk(clk_out), .Q(cpu_out[47:32]), .clr(reset_out));
  add_sixteen add_sixteen_1 (
    .AddSub(1'b0), .A(cpu_out[47:32]), .B(multiplexer_1_out), .S(add_sixteen_1_s));  // open: Overflow, Cout
  ROM #(.addrWidth(16), .dataWidth(16)) InsMem (.addr(cpu_out[47:32]), .data(InsMem_data));
  Decoder #(.enable("false"), .select(3)) decoder_1 (
    .out0(decoder_1_out0), .out1(decoder_1_out1), .out2(decoder_1_out2), .out3(decoder_1_out3),
    .out4(decoder_1_out4), .sel(register_1_q));  // open: out5, out6, out7
  and and_2 (and_2_out, decoder_1_out2, decoder_2_out1, multiplexer_5_out);
  // Probe on clk_out
  and and_3 (and_3_out, decoder_1_out4, nor_1_out);
  Register #(.width(16)) IR (.D(InsMem_data), .en(decoder_1_out0), .clk(clk_out), .Q(cpu_out[31:16]), .clr(reset_out));
  // Probe on cpu_out[29:27]
  nor nor_1 (nor_1_out, decoder_2_out1, decoder_2_out3);
  Multiplexer #(.width(3)) multiplexer_2 (
    .in0(cpu_out[18:16]), .in1(cpu_out[25:23]), .out(multiplexer_2_out), .sel(decoder_2_out3));
  Comparator #(.width(16)) comparator_1 (.a(cpu_out[31:16]), .b(16'h4380), .eq(halt));  // open: gt, lt
  Decoder #(.enable("false"), .select(2)) decoder_2 (
    .out1(decoder_2_out1), .out2(decoder_2_out2), .out3(decoder_2_out3), .sel(cpu_out[31:30]));  // open: out0
  // Probe on cpu_out[31:16]
  Register #(.width(16)) RA (.D(registerfile_1_a), .en(decoder_1_out1), .clk(clk_out), .Q(RA_q), .clr(reset_out));
  RegisterFile registerfile_1 (
    .Addr_A(cpu_out[22:20]), .Addr_B(multiplexer_2_out), .Addr_C(cpu_out[25:23]), .we(and_3_out),
    .clk(clk_out), .reset(reset_out), .C(RW_q), .A(registerfile_1_a), .B(registerfile_1_b));
  Register #(.width(16)) RB (.D(registerfile_1_b), .en(decoder_1_out1), .clk(clk_out), .Q(RB_q), .clr(reset_out));
  assign bit_extender_3_out = {{12{cpu_out[19]}}, cpu_out[19:16]};  // Bit_Extender bit_extender_3
  Multiplexer #(.width(16)) multiplexer_3 (
    .in0(RB_q), .in1(bit_extender_3_out), .out(multiplexer_3_out), .sel(cpu_out[26]));
  // Probe on RA_q
  // Probe on multiplexer_3_out
  not not_2 (not_2_out, alu_1_zero);
  Multiplexer #(.width(3)) multiplexer_4 (
    .in0(cpu_out[29:27]), .in1(3'b001), .out(multiplexer_4_out), .sel(decoder_2_out1));
  ALU alu_1 (
    .A(RA_q), .B(multiplexer_3_out), .fun(multiplexer_4_out), .negative(alu_1_negative), .zero(alu_1_zero),
    .overflow(alu_1_overflow), .C(alu_1_c));  // open: carry
  xor xor_1 (xor_1_out, alu_1_negative, alu_1_overflow);
  or or_2 (or_2_out, alu_1_zero, xor_1_out);
  not not_3 (not_3_out, or_2_out);
  not not_4 (not_4_out, xor_1_out);
  Multiplexer #(.select(3)) multiplexer_5 (
    .in0(alu_1_zero), .in1(not_2_out), .in2(xor_1_out), .in3(or_2_out), .in4(not_3_out), .in5(not_4_out),
    .out(multiplexer_5_out));  // open: in6, in7, sel
  // Probe on alu_1_c
  Register #(.width(16)) RD (.D(RB_q), .en(decoder_1_out2), .clk(clk_out), .Q(RD_q), .clr(reset_out));
  Register #(.width(16)) RZ (.D(alu_1_c), .en(decoder_1_out2), .clk(clk_out), .Q(cpu_out[15:0]), .clr(reset_out));
  and and_4 (and_4_out, decoder_1_out3, decoder_2_out3);
  // Probe on cpu_out[15:0]
  Multiplexer #(.width(16)) multiplexer_6 (
    .in0(cpu_out[15:0]), .in1(ram_1_dout), .out(multiplexer_6_out), .sel(decoder_2_out2));
  Register #(.width(16)) RW (.D(multiplexer_6_out), .en(decoder_1_out3), .clk(clk_out), .Q(RW_q), .clr(reset_out));
  RAM #(.addrWidth(16), .dataWidth(16), .enables("line")) ram_1 (
    .addr(cpu_out[15:0]), .we(and_4_out), .clk(clk_out), .din(RD_q), .dout(ram_1_dout));

  // Notes on the sheet:
  //   contents of InsMem (hex, n*v repeats v):
  //   493 6d90 2091 491 401 52d 6da0 2122 521 401 15b0 16d0 1621 4540 4e50 1b1 2c91 4e50 3521 2d2 4e50
  //   4d01 21b3 5b1 5b0 4380
  //   FSM
  //   execute && branch taken
  //   ALU
  //   Branching
  //   is_store
  //   is_load
  //   branch condition is true
  //   subtract when branching
endmodule

module ALU (
  input  [2:0] fun,
  input  [15:0] A,
  input  [15:0] B,
  output [15:0] C,
  output negative,
  output zero,
  output carry,
  output overflow
);

  wire [15:0] add_sixteen_1_s, and_1_out, nor_1_out, or_1_out, shifter_1_out, shifter_2_out, shifter_3_out;

  add_sixteen add_sixteen_1 (.AddSub(fun[0]), .A(A), .B(B), .S(add_sixteen_1_s), .Overflow(overflow), .Cout(carry));
  assign and_1_out = A & B;  // AND_Gate and_1, 16 bits wide
  assign or_1_out = A | B;  // OR_Gate or_1, 16 bits wide
  assign nor_1_out = ~(A | B);  // NOR_Gate nor_1, 16 bits wide
  Shifter #(.width(16)) shifter_1 (.in(A), .\dist (B[3:0]), .out(shifter_1_out));
  Shifter #(.shift("lr"), .width(16)) shifter_2 (.in(A), .\dist (B[3:0]), .out(shifter_2_out));
  Shifter #(.shift("ar"), .width(16)) shifter_3 (.in(A), .\dist (B[3:0]), .out(shifter_3_out));
  Multiplexer #(.select(3), .width(16)) multiplexer_1 (
    .in0(add_sixteen_1_s), .in1(add_sixteen_1_s), .in2(and_1_out), .in3(or_1_out), .in4(nor_1_out),
    .in5(shifter_1_out), .in6(shifter_2_out), .in7(shifter_3_out), .out(C), .sel(fun));
  Comparator #(.width(16)) comparator_1 (.a(C), .b({16{1'b0}}), .eq(zero), .lt(negative));  // open: gt
endmodule

module RegisterFile (
  input  [2:0] Addr_A,
  input  [2:0] Addr_B,
  input  [2:0] Addr_C,
  input  we,
  input  clk,
  input  reset,
  input  [15:0] C,
  output [15:0] A,
  output [15:0] B
);

  wire demultiplexer_1_out0, demultiplexer_1_out1, demultiplexer_1_out2, demultiplexer_1_out3,
       demultiplexer_1_out4, demultiplexer_1_out5, demultiplexer_1_out6, demultiplexer_1_out7;
  wire [15:0] R0_q, R1_q, R2_q, R3_q, R4_q, R5_q, R6_q, R7_q;

  Demultiplexer #(.select(3)) demultiplexer_1 (
    .out0(demultiplexer_1_out0), .out1(demultiplexer_1_out1), .out2(demultiplexer_1_out2),
    .out3(demultiplexer_1_out3), .out4(demultiplexer_1_out4), .out5(demultiplexer_1_out5),
    .out6(demultiplexer_1_out6), .out7(demultiplexer_1_out7), .in(we), .sel(Addr_C));
  Register #(.width(16)) R0 (.D(C), .en(demultiplexer_1_out0), .clk(clk), .Q(R0_q), .clr(reset));
  Register #(.width(16)) R1 (.D(C), .en(demultiplexer_1_out1), .clk(clk), .Q(R1_q), .clr(reset));
  Register #(.width(16)) R2 (.D(C), .en(demultiplexer_1_out2), .clk(clk), .Q(R2_q), .clr(reset));
  Register #(.width(16)) R3 (.D(C), .en(demultiplexer_1_out3), .clk(clk), .Q(R3_q), .clr(reset));
  Register #(.width(16)) R4 (.D(C), .en(demultiplexer_1_out4), .clk(clk), .Q(R4_q), .clr(reset));
  Register #(.width(16)) R5 (.D(C), .en(demultiplexer_1_out5), .clk(clk), .Q(R5_q), .clr(reset));
  Register #(.width(16)) R6 (.D(C), .en(demultiplexer_1_out6), .clk(clk), .Q(R6_q), .clr(reset));
  Register #(.width(16)) R7 (.D(C), .en(demultiplexer_1_out7), .clk(clk), .Q(R7_q), .clr(reset));
  Multiplexer #(.select(3), .width(16)) multiplexer_1 (
    .in0(R0_q), .in1(R1_q), .in2(R2_q), .in3(R3_q), .in4(R4_q), .in5(R5_q), .in6(R6_q), .in7(R7_q), .out(A),
    .sel(Addr_A));
  Multiplexer #(.select(3), .width(16)) multiplexer_2 (
    .in0(R0_q), .in1(R1_q), .in2(R2_q), .in3(R3_q), .in4(R4_q), .in5(R5_q), .in6(R6_q), .in7(R7_q), .out(B),
    .sel(Addr_B));
endmodule

module RegisterFileTester (
  output halt,
  output [15:0] A,
  output [15:0] B,
  output clk
);

  wire undriven;
  wire [2:0] Addr_A_data, Addr_B_data, Addr_C_data;
  wire [3:0] adder_1_out, addr_q;
  wire [15:0] C_data;

  Clock clock_1 (.out(clk));
  ROM #(.addrWidth(4), .dataWidth(3)) Addr_A (.addr(addr_q), .data(Addr_A_data));
  ROM #(.addrWidth(4), .dataWidth(3)) Addr_B (.addr(addr_q), .data(Addr_B_data));
  ROM #(.addrWidth(4), .dataWidth(3)) Addr_C (.addr(addr_q), .data(Addr_C_data));
  ROM #(.addrWidth(4), .dataWidth(1)) we (.addr(addr_q));  // open: data
  ROM #(.addrWidth(4), .dataWidth(16)) C (.addr(addr_q), .data(C_data));
  Adder #(.width(4)) adder_1 (.a(addr_q), .b(4'b0001), .out(adder_1_out), .cin(1'b0));  // open: cout
  Register #(.width(4)) addr (.D(adder_1_out), .en(1'b1), .clk(clk), .Q(addr_q), .clr(1'b0));
  Comparator #(.width(4)) comparator_1 (.a(addr_q), .b(4'b1111), .eq(halt));  // open: gt, lt
  RegisterFile registerfile_1 (
    .Addr_A(Addr_A_data), .Addr_B(Addr_B_data), .Addr_C(Addr_C_data), .we(undriven), .clk(clk), .reset(1'b0),
    .C(C_data), .A(A), .B(B));

  // Notes on the sheet:
  //   contents of Addr_A (hex, n*v repeats v):
  //   5 2 7 3 2 0 2 6 2 4 1 3 5 5 2 6
  //   contents of Addr_B (hex, n*v repeats v):
  //   4 4 6 0 2 3 5 5 5 0 0 4 5 3 7 5
  //   contents of Addr_C (hex, n*v repeats v):
  //   0 5 0 5 5 7 2 3 6 4 0 4 7 7 4 6
  //   contents of we (hex, n*v repeats v):
  //   0 0 0 1 0 0 1 0 0 0 1 1 0 0 1 1
  //   contents of C (hex, n*v repeats v):
  //   1 4 c f 0 5 9 7 c b 9 f b 9 1 e
endmodule

module fulladder (
  input  A,
  input  B,
  input  Cin,
  output S,
  output Cout
);

  wire and_1_out, and_2_out, xor_1_out;

  xor xor_1 (xor_1_out, A, B);
  and and_1 (and_1_out, xor_1_out, Cin);
  and and_2 (and_2_out, A, B);
  xor xor_2 (S, xor_1_out, Cin);
  or or_1 (Cout, and_1_out, and_2_out);
endmodule

module add_eight (
  input  Cin,
  input  [7:0] A,
  input  [7:0] B,
  output [7:0] C,
  output overflow,
  output Cout
);

  wire fulladder_1_cout, fulladder_2_cout, fulladder_3_cout, fulladder_4_cout, fulladder_5_cout,
       fulladder_6_cout, fulladder_7_cout;

  fulladder fulladder_1 (.A(A[0]), .B(B[0]), .Cin(Cin), .S(C[0]), .Cout(fulladder_1_cout));
  fulladder fulladder_2 (.A(A[1]), .B(B[1]), .Cin(fulladder_1_cout), .S(C[1]), .Cout(fulladder_2_cout));
  fulladder fulladder_3 (.A(A[2]), .B(B[2]), .Cin(fulladder_2_cout), .S(C[2]), .Cout(fulladder_3_cout));
  fulladder fulladder_4 (.A(A[3]), .B(B[3]), .Cin(fulladder_3_cout), .S(C[3]), .Cout(fulladder_4_cout));
  fulladder fulladder_5 (.A(A[4]), .B(B[4]), .Cin(fulladder_4_cout), .S(C[4]), .Cout(fulladder_5_cout));
  fulladder fulladder_6 (.A(A[5]), .B(B[5]), .Cin(fulladder_5_cout), .S(C[5]), .Cout(fulladder_6_cout));
  fulladder fulladder_7 (.A(A[6]), .B(B[6]), .Cin(fulladder_6_cout), .S(C[6]), .Cout(fulladder_7_cout));
  fulladder fulladder_8 (.A(A[7]), .B(B[7]), .Cin(fulladder_7_cout), .S(C[7]), .Cout(Cout));
  xor xor_1 (overflow, fulladder_7_cout, Cout);
endmodule

module add_sixteen (
  input  AddSub,
  input  [15:0] A,
  input  [15:0] B,
  output [15:0] S,
  output Overflow,
  output Cout
);

  wire add_eight_1_cout;
  wire [15:0] bit_extender_1_out, xor_1_out;

  assign bit_extender_1_out = {{15{AddSub}}, AddSub};  // Bit_Extender bit_extender_1
  assign xor_1_out = bit_extender_1_out ^ B;  // XOR_Gate xor_1, 16 bits wide
  add_eight add_eight_1 (
    .Cin(AddSub), .A(A[7:0]), .B(xor_1_out[7:0]), .C(S[7:0]), .Cout(add_eight_1_cout));  // open: overflow
  add_eight add_eight_2 (
    .Cin(add_eight_1_cout), .A(A[15:8]), .B(xor_1_out[15:8]), .C(S[15:8]), .overflow(Overflow), .Cout(Cout));
endmodule
